# Fritzing sketch Robot (saved by Fritzing 0.9.3b)

parts:
  Part3 = NRF24L01+ Breakout Board
  Part4 = Arduino Nano (Rev3.0)
  L298N1 = L298N DC motor driver
  U1 = SWITCH_SPDT [package=kps-1290]
  VCC1 = Battery block 9V
  M1 = DC Motor
  M2 = DC Motor

nets:
  GND: Part3.GND, Part4.GND
  VCC: Part3.VCC, Part4.3V3
  N1: Part3.CE, Part4.D7
  N2: Part3.CS, Part4.D8
  N3: Part3.SCK, Part4.D13/SCK
  N4: Part3.MOSI, Part4.D11/MOSI
  N5: Part3.MISO, Part4.D12/MISO
  N6: Part4.D3, L298N1.ENB
  N7: Part4.D5, L298N1.ENA
  VIN: Part4.VIN, L298N1.5V
  N8: Part4.A3, L298N1.IN4
  N9: Part4.A2, L298N1.IN3
  N10: Part4.A1, L298N1.IN2
  N11: Part4.A0, L298N1.IN1
  N12: L298N1.OUT1, M2.pin_2
  N13: L298N1.OUT2, M2.pin_1
  N14: L298N1.OUT3, M1.pin_2
  N15: L298N1.OUT4, M1.pin_1
  N16: L298N1.12V, U1.O
  N17: L298N1.GND, VCC1.-
  N18: U1.S, VCC1.+

custom parts:
  L298N DC motor driver: 2x DC motor driver with 78M05 positive voltage regulator (7..35 V) L298N: max 46 V, 2 A Set 5 V Enable jumper to enable 5 V regultor (needed for the L298N) and +5 V output at screw terminal or supply external +5 V at screw terminal Set ENA and/or ENB to +5 V to enable motor permanently or supply ENA and/or ENB with PWM signal IN1 and IN2 set rotation directory for motor A (OUT1/OUT2) IN2 and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
