# Fritzing sketch Sender (saved by Fritzing 0.9.3b)

parts:
  Part1 = NRF24L01+ Breakout Board
  Part2 = Arduino Nano (Rev3.0)

nets:
  GND: Part1.GND, Part2.GND
  VCC: Part1.VCC, Part2.3V3
  N1: Part1.CE, Part2.D7
  N2: Part1.CS, Part2.D8
  N3: Part1.SCK, Part2.D13/SCK
  N4: Part1.MOSI, Part2.D11/MOSI
  N5: Part1.MISO, Part2.D12/MISO
